// Logisim project arquitetura_de_computadores_29_02_2024.circ as structural Verilog: 8 circuits, main circuit main
module main (
  input  [3:0] A,
  input  [3:0] B,
  input  [2:0] in_3,
  output out_4,
  output out_5,
  output [3:0] s
);

  wire decoder_3x8_1_s0, decoder_3x8_1_s1, decoder_3x8_1_s2, decoder_3x8_1_s4;
  wire [3:0] ad_4_1_out_5, sub_4_1_out_5;

  BUFFER buffer_1 (.in_2(decoder_3x8_1_s0), .B(B), .S(s));
  DECODER_3x8 decoder_3x8_1 (
    .S0(decoder_3x8_1_s0), .S1(decoder_3x8_1_s1), .S2(decoder_3x8_1_s2), .S4(decoder_3x8_1_s4), .in_1(in_3));  // open: S3, S5, S6, S7
  AD_4 ad_4_1 (.in_2(A), .out_4(out_4), .in_1(B), .in_3(1'b0), .out_5(ad_4_1_out_5));
  BUFFER buffer_2 (.in_2(decoder_3x8_1_s1), .B(ad_4_1_out_5), .S(s));
  SUB_4 sub_4_1 (.in_2(A), .out_4(out_5), .in_1(B), .in_3(1'b0), .out_5(sub_4_1_out_5));
  BUFFER buffer_3 (.in_2(decoder_3x8_1_s2), .B(sub_4_1_out_5), .S(s));
  BUFFER_CONTROLADO_INVERTIDO buffer_controlado_invertido_1 (.in_2(decoder_3x8_1_s4), .S(s), .B(B));
endmodule

module AD_1 (
  input  A,
  input  B,
  input  Vem_1,
  output S,
  output Vai_1
);

  wire and_1_out, and_2_out, or_1_out, xor_1_out;

  xor xor_1 (xor_1_out, A, B);
  or or_1 (or_1_out, Vem_1, B);
  and and_1 (and_1_out, Vem_1, B);
  xor xor_2 (S, xor_1_out, Vem_1);
  and and_2 (and_2_out, or_1_out, A);
  or or_2 (Vai_1, and_2_out, and_1_out);
endmodule

module AD_4 (
  input  [3:0] in_1,
  input  [3:0] in_2,
  input  in_3,
  output out_4,
  output [3:0] out_5
);

  wire ad_1_2_vai_1, ad_1_3_vai_1, ad_1_4_vai_1;

  AD_1 ad_1_1 (.A(in_2[3]), .B(in_1[3]), .S(out_5[3]), .Vem_1(ad_1_2_vai_1), .Vai_1(out_4));
  AD_1 ad_1_2 (.A(in_2[2]), .B(in_1[2]), .S(out_5[2]), .Vem_1(ad_1_3_vai_1), .Vai_1(ad_1_2_vai_1));
  AD_1 ad_1_3 (.A(in_2[1]), .B(in_1[1]), .S(out_5[1]), .Vem_1(ad_1_4_vai_1), .Vai_1(ad_1_3_vai_1));
  AD_1 ad_1_4 (.A(in_2[0]), .B(in_1[0]), .S(out_5[0]), .Vem_1(in_3), .Vai_1(ad_1_4_vai_1));
endmodule

module SUB_1 (
  input  A,
  input  B,
  input  Vem_1,
  output S,
  output Vai_1
);

  wire and_1_out, and_2_out, not_1_out, or_1_out, xor_1_out;

  not not_1 (not_1_out, A);
  xor xor_1 (xor_1_out, A, B);
  or or_1 (or_1_out, Vem_1, B);
  and and_1 (and_1_out, Vem_1, B);
  xor xor_2 (S, xor_1_out, Vem_1);
  and and_2 (and_2_out, or_1_out, not_1_out);
  or or_2 (Vai_1, and_2_out, and_1_out);
endmodule

module SUB_4 (
  input  [3:0] in_1,
  input  [3:0] in_2,
  input  in_3,
  output out_4,
  output [3:0] out_5
);

  wire sub_1_2_vai_1, sub_1_3_vai_1, sub_1_4_vai_1;

  SUB_1 sub_1_1 (.A(in_2[3]), .B(in_1[3]), .Vem_1(sub_1_2_vai_1), .S(out_5[3]), .Vai_1(out_4));
  SUB_1 sub_1_2 (.A(in_2[2]), .B(in_1[2]), .Vem_1(sub_1_3_vai_1), .S(out_5[2]), .Vai_1(sub_1_2_vai_1));
  SUB_1 sub_1_3 (.A(in_2[1]), .B(in_1[1]), .Vem_1(sub_1_4_vai_1), .S(out_5[1]), .Vai_1(sub_1_3_vai_1));
  SUB_1 sub_1_4 (.A(in_2[0]), .B(in_1[0]), .Vem_1(in_3), .S(out_5[0]), .Vai_1(sub_1_4_vai_1));
endmodule

module BUFFER (
  input  [3:0] B,
  input  in_2,
  output [3:0] S
);

  assign S[3] = in_2 ? B[3] : 1'bz;  // Controlled_Buffer controlled_buffer_1
  assign S[2] = in_2 ? B[2] : 1'bz;  // Controlled_Buffer controlled_buffer_2
  assign S[0] = in_2 ? B[0] : 1'bz;  // Controlled_Buffer controlled_buffer_3
  assign S[1] = in_2 ? B[1] : 1'bz;  // Controlled_Buffer controlled_buffer_4
endmodule

module BUFFER_CONTROLADO_INVERTIDO (
  input  [3:0] B,
  input  in_2,
  output [3:0] S
);

  assign S[2] = in_2 ? ~B[2] : 1'bz;  // Controlled_Inverter controlled_inverter_1
  assign S[3] = in_2 ? ~B[3] : 1'bz;  // Controlled_Inverter controlled_inverter_2
  assign S[0] = in_2 ? ~B[0] : 1'bz;  // Controlled_Inverter controlled_inverter_3
  assign S[1] = in_2 ? ~B[1] : 1'bz;  // Controlled_Inverter controlled_inverter_4
endmodule

module DECODER_3x8 (
  input  [2:0] in_1,
  output S0,
  output S1,
  output S2,
  output S3,
  output S4,
  output S5,
  output S6,
  output S7
);

  wire not_1_out, not_2_out, not_3_out, not_4_out, not_5_out, not_6_out, not_7_out, not_8_out, not_9_out,
       not_10_out, not_11_out, not_12_out;

  not not_1 (not_1_out, in_1[2]);
  not not_2 (not_2_out, in_1[1]);
  not not_3 (not_3_out, in_1[0]);
  not not_4 (not_4_out, in_1[2]);
  not not_5 (not_5_out, in_1[1]);
  not not_6 (not_6_out, in_1[2]);
  not not_7 (not_7_out, in_1[0]);
  not not_8 (not_8_out, in_1[2]);
  not not_9 (not_9_out, in_1[1]);
  not not_10 (not_10_out, in_1[0]);
  not not_11 (not_11_out, in_1[1]);
  not not_12 (not_12_out, in_1[0]);
  and and_1 (S7, in_1[2], in_1[1], in_1[0]);
  and and_2 (S0, not_1_out, not_2_out, not_3_out);
  and and_3 (S1, not_4_out, not_5_out, in_1[0]);
  and and_4 (S2, not_6_out, in_1[1], not_7_out);
  and and_5 (S3, not_8_out, in_1[1], in_1[0]);
  and and_6 (S4, in_1[2], not_9_out, not_10_out);
  and and_7 (S5, in_1[2], not_11_out, in_1[0]);
  and and_8 (S6, in_1[2], in_1[1], not_12_out);
endmodule
